// Logisim project 24_bits.circ as structural Verilog: 6 circuits, main circuit main
module test (
  input  [4:0] in_1,
  output [23:0] out_2,
  output [23:0] out_3,
  output out_4,
  output [23:0] out_5,
  output [23:0] out_6,
  output [23:0] out_7
);

  wire alucon_1_out_9, and_1_out, clock_1_out, controlunit_1__1_2, controlunit_1__2_2, controlunit_1__3_2,
       controlunit_1__4, controlunit_1__5, controlunit_1__6, controlunit_1__7, controlunit_1__8,
       controlunit_1__9, controlunit_1__10;
  wire [1:0] alucon_1_out_11;
  wire [3:0] multiplexer_1_out;
  wire [11:0] rom_1_data_2;
  wire [19:12] rom_1_data_3;
  wire [23:0] adder_1_out, adder_2_out, bit_extender_1_out, multiplexer_2_out, multiplexer_3_out, ram_1_data,
       register_1_q, shifter_1_out;
  wire [23:20] rom_1_data;

  Register #(.width(24)) register_1 (.D(out_2), .Q(register_1_q), .clk(clock_1_out));  // open: en, clr
  Clock clock_1 (.out(clock_1_out));
  Adder #(.width(24)) adder_1 (.a(register_1_q), .b(24'h1), .out(adder_1_out));  // open: cin, cout
  ROM #(.addrWidth(24), .dataWidth(24)) rom_1 (
    .addr(register_1_q), .data({rom_1_data, rom_1_data_3, rom_1_data_2}));  // open: sel
  assign bit_extender_1_out = {{12{rom_1_data_2[11]}}, rom_1_data_2};  // Bit_Extender bit_extender_1
  Multiplexer #(.width(4), .enable("false")) multiplexer_1 (
    .in0(rom_1_data_3[15:12]), .in1(rom_1_data_2[11:8]), .out(multiplexer_1_out), .sel(controlunit_1__1_2));
  CONTROLUNIT controlunit_1 (
    ._1_2(controlunit_1__1_2), ._2_2(controlunit_1__2_2), ._3_2(controlunit_1__3_2), ._4(controlunit_1__4),
    ._5(controlunit_1__5), ._6(controlunit_1__6), ._7(controlunit_1__7), ._8(controlunit_1__8),
    ._9(controlunit_1__9), ._10(controlunit_1__10), ._3(rom_1_data[23]), ._2(rom_1_data[22]),
    ._1(rom_1_data[21]), ._0(rom_1_data[20]));
  RegFile regfile_1 (
    .in_1(out_5), .write_data(controlunit_1__2_2), .out_7(out_3), .out_8(out_6), .in_4(multiplexer_1_out),
    .clk(clock_1_out), .in_5(rom_1_data_3[15:12]), .in_3(rom_1_data_3[19:16]));
  ALUCON alucon_1 (
    ._0(rom_1_data_2[4]), .out_9(alucon_1_out_9), .out_10(alucon_1_out_11[1]), .out_11(alucon_1_out_11[0]),
    .in_2(controlunit_1__9), .in_3(controlunit_1__10), .F3(rom_1_data_2[3]), .F2(rom_1_data_2[2]),
    .F1(rom_1_data_2[1]), .F0(rom_1_data_2[0]));  // open: out_8
  Multiplexer #(.width(24), .enable("false")) multiplexer_2 (
    .in0(out_6), .in1(bit_extender_1_out), .out(multiplexer_2_out), .sel(controlunit_1__3_2));
  Shifter #(.width(24)) shifter_1 (.in(bit_extender_1_out), .\dist (in_1), .out(shifter_1_out));
  Adder #(.width(24)) adder_2 (.a(adder_1_out), .b(shifter_1_out), .out(adder_2_out));  // open: cin, cout
  ALU alu_1 (
    .in_1(out_3), .in_2(multiplexer_2_out), .Zero_Flag(out_4), .out_6(out_7), .B_Invert(alucon_1_out_9),
    .ALU_Control_Bits(alucon_1_out_11));
  Multiplexer #(.width(24), .enable("false")) multiplexer_3 (
    .in0(adder_1_out), .in1(adder_2_out), .out(multiplexer_3_out), .sel(and_1_out));
  and and_1 (and_1_out, controlunit_1__7, out_4);
  Multiplexer #(.width(24), .enable("false")) multiplexer_4 (
    .in0(multiplexer_3_out), .in1({adder_1_out[23:20], rom_1_data_3, rom_1_data_2}), .out(out_2),
    .sel(controlunit_1__8));
  Multiplexer #(.width(24), .enable("false")) multiplexer_5 (
    .in0(out_7), .in1(ram_1_data), .out(out_5), .sel(controlunit_1__6));
  RAM #(.addrWidth(24), .dataWidth(24), .bus("separate")) ram_1 (
    .addr(out_7), .din(out_6), .data(ram_1_data), .str(controlunit_1__5), .clk(clock_1_out),
    .ld(controlunit_1__4));  // open: sel, clr

  // Notes on the sheet:
  //   FN
  //   contents of rom_1 (hex, n*v repeats v):
  //   0 413004 100003 100007 0 100002 250*0 100004
  //   OP
endmodule

module ALU (
  input  [23:0] in_1,
  input  [23:0] in_2,
  input  [1:0] ALU_Control_Bits,
  input  B_Invert,
  output Zero_Flag,
  output [23:0] out_6
);

  wire [23:0] adder_1_out, and_1_out, multiplexer_1_out, not_1_out, or_1_out;

  assign not_1_out = ~in_2;  // NOT_Gate not_1, 24 bits wide
  Multiplexer #(.width(24), .enable("false")) multiplexer_1 (
    .in0(in_2), .in1(not_1_out), .out(multiplexer_1_out), .sel(B_Invert));
  assign and_1_out = in_1 & in_2;  // AND_Gate and_1, 24 bits wide
  assign or_1_out = in_1 | in_2;  // OR_Gate or_1, 24 bits wide
  Adder #(.width(24)) adder_1 (.a(in_1), .b(multiplexer_1_out), .out(adder_1_out), .cin(B_Invert));  // open: cout
  Multiplexer #(.select(2), .width(24), .enable("false")) multiplexer_2 (
    .in0(and_1_out), .in1(or_1_out), .in2(adder_1_out), .out(out_6), .sel(ALU_Control_Bits));  // open: in3
  nor nor_1 (Zero_Flag, out_6[0], out_6[1], out_6[2], out_6[3], out_6[4], out_6[5], out_6[6], out_6[7], out_6[8], out_6[9], out_6[10], out_6[11], out_6[12], out_6[13], out_6[14], out_6[15], out_6[16], out_6[17], out_6[18], out_6[19], out_6[20], out_6[21], out_6[22], out_6[23]);

  // Notes on the sheet:
  //   Read Data 1
  //   Read Data 2
  //   For Subtraction
  //   ALU Result
endmodule

module RegFile (
  input  [23:0] in_1,
  input  write_data,
  input  [3:0] in_3,
  input  [3:0] in_4,
  input  [3:0] in_5,
  input  clk,
  output [23:0] out_7,
  output [23:0] out_8
);

  wire and_1_out, and_2_out, and_3_out, and_4_out, and_5_out, and_6_out, and_7_out, and_8_out, and_9_out,
       and_10_out, and_11_out, and_12_out, and_13_out, and_14_out, and_15_out, and_16_out, decoder_1_out0,
       decoder_1_out1, decoder_1_out2, decoder_1_out3, decoder_1_out4, decoder_1_out5, decoder_1_out6,
       decoder_1_out7, decoder_1_out8, decoder_1_out9, decoder_1_out10, decoder_1_out11, decoder_1_out12,
       decoder_1_out13, decoder_1_out14, decoder_1_out15;
  wire [23:0] register_1_q, register_2_q, register_3_q, register_4_q, register_5_q, register_6_q,
       register_7_q, register_8_q, register_9_q, register_10_q, register_11_q, register_12_q, register_13_q,
       register_14_q, register_15_q, register_16_q, undriven;

  Decoder #(.select(4), .enable("false")) decoder_1 (
    .out0(decoder_1_out0), .out1(decoder_1_out1), .out2(decoder_1_out2), .out3(decoder_1_out3),
    .out4(decoder_1_out4), .out5(decoder_1_out5), .out6(decoder_1_out6), .out7(decoder_1_out7),
    .out8(decoder_1_out8), .out9(decoder_1_out9), .out10(decoder_1_out10), .out11(decoder_1_out11),
    .out12(decoder_1_out12), .out13(decoder_1_out13), .out14(decoder_1_out14), .out15(decoder_1_out15),
    .sel(in_4));
  and and_1 (and_1_out, write_data, decoder_1_out0);
  and and_2 (and_2_out, write_data, decoder_1_out1);
  and and_3 (and_3_out, write_data, decoder_1_out2);
  and and_4 (and_4_out, write_data, decoder_1_out3);
  and and_5 (and_5_out, write_data, decoder_1_out4);
  and and_6 (and_6_out, write_data, decoder_1_out5);
  and and_7 (and_7_out, write_data, decoder_1_out6);
  and and_8 (and_8_out, write_data, decoder_1_out7);
  and and_9 (and_9_out, write_data, decoder_1_out8);
  and and_10 (and_10_out, write_data, decoder_1_out9);
  and and_11 (and_11_out, write_data, decoder_1_out10);
  and and_12 (and_12_out, write_data, decoder_1_out11);
  and and_13 (and_13_out, write_data, decoder_1_out12);
  and and_14 (and_14_out, write_data, decoder_1_out13);
  and and_15 (and_15_out, write_data, decoder_1_out14);
  and and_16 (and_16_out, write_data, decoder_1_out15);
  Register #(.width(24)) register_1 (.D(in_1), .en(and_1_out), .Q(register_1_q), .clk(clk));  // open: clr
  Register #(.width(24)) register_2 (.D(in_1), .en(and_2_out), .Q(register_2_q), .clk(clk));  // open: clr
  Register #(.width(24)) register_3 (.D(in_1), .en(and_3_out), .Q(register_3_q), .clk(clk));  // open: clr
  Register #(.width(24)) register_4 (.D(in_1), .en(and_4_out), .Q(register_4_q), .clk(clk));  // open: clr
  Register #(.width(24)) register_5 (.D(in_1), .en(and_5_out), .Q(register_5_q), .clk(clk));  // open: clr
  Register #(.width(24)) register_6 (.D(in_1), .en(and_6_out), .Q(register_6_q), .clk(clk));  // open: clr
  Register #(.width(24)) register_7 (.D(in_1), .en(and_7_out), .Q(register_7_q), .clk(clk));  // open: clr
  Register #(.width(24)) register_8 (.D(in_1), .en(and_8_out), .Q(register_8_q), .clk(clk));  // open: clr
  Register #(.width(24)) register_9 (.D(undriven), .en(and_9_out), .Q(register_9_q), .clk(clk));  // open: clr
  Register #(.width(24)) register_10 (.D(undriven), .en(and_10_out), .Q(register_10_q), .clk(clk));  // open: clr
  Register #(.width(24)) register_11 (.D(undriven), .en(and_11_out), .Q(register_11_q), .clk(clk));  // open: clr
  Register #(.width(24)) register_12 (.D(undriven), .en(and_12_out), .Q(register_12_q), .clk(clk));  // open: clr
  Register #(.width(24)) register_13 (.D(undriven), .en(and_13_out), .Q(register_13_q), .clk(clk));  // open: clr
  Register #(.width(24)) register_14 (.D(undriven), .en(and_14_out), .Q(register_14_q), .clk(clk));  // open: clr
  Register #(.width(24)) register_15 (.D(undriven), .en(and_15_out), .Q(register_15_q), .clk(clk));  // open: clr
  Register #(.width(24)) register_16 (.D(undriven), .en(and_16_out), .Q(register_16_q), .clk(clk));  // open: clr
  Multiplexer #(.select(4), .width(24), .enable("false")) multiplexer_1 (
    .in0(register_1_q), .in1(register_2_q), .in2(register_3_q), .in3(register_4_q), .in4(register_5_q),
    .in5(register_6_q), .in6(register_7_q), .in7(register_8_q), .in8(register_9_q), .in9(register_10_q),
    .in10(register_11_q), .in11(register_12_q), .in12(register_13_q), .in13(register_14_q),
    .in14(register_15_q), .in15(register_16_q), .out(out_7), .sel(in_3));
  Multiplexer #(.select(4), .width(24), .enable("false")) multiplexer_2 (
    .in0(register_1_q), .in1(register_2_q), .in2(register_3_q), .in3(register_4_q), .in4(register_5_q),
    .in5(register_6_q), .in6(register_7_q), .in7(register_8_q), .in8(register_9_q), .in9(register_10_q),
    .in10(register_11_q), .in11(register_12_q), .in12(register_13_q), .in13(register_14_q),
    .in14(register_15_q), .in15(register_16_q), .out(out_8), .sel(in_5));

  // Notes on the sheet:
  //   RegWrite
  //   write register
  //   Read Register 1
  //   Read Register 2
  //   Data 1
  //   Data 2
endmodule

module ALUCON (
  input  _0,
  input  in_2,
  input  in_3,
  input  F3,
  input  F2,
  input  F1,
  input  F0,
  output out_8,
  output out_9,
  output out_10,
  output out_11
);

  wire and_1_out, and_2_out, not_1_out;

  not not_1 (not_1_out, in_2);
  and and_1 (and_1_out, in_2, F2);
  and and_2 (and_2_out, in_2, F1);
  and and_3 (out_11, in_2, F0);
  or or_1 (out_9, in_3, and_1_out);
  or or_2 (out_10, not_1_out, and_2_out);

  assign out_8 = _0;

  // Notes on the sheet:
  //   ALUOP1
  //   ALUOP0
endmodule

module CONTROLUNIT (
  input  _3,
  input  _2,
  input  _1,
  input  _0,
  output _1_2,
  output _2_2,
  output _3_2,
  output _4,
  output _5,
  output _6,
  output _7,
  output _8,
  output _9,
  output _10
);

  wire not_1_out, not_2_out, not_3_out, not_4_out, not_5_out, not_6_out, not_7_out, not_8_out, not_9_out,
       not_10_out, not_11_out, not_12_out, not_13_out, not_14_out, not_15_out, not_16_out;

  not not_1 (not_1_out, _3);
  not not_2 (not_2_out, _2);
  not not_3 (not_3_out, _1);
  not not_4 (not_4_out, _0);
  not not_5 (not_5_out, _2);
  not not_6 (not_6_out, _1);
  not not_7 (not_7_out, _0);
  not not_8 (not_8_out, _3);
  not not_9 (not_9_out, _1);
  not not_10 (not_10_out, _0);
  not not_11 (not_11_out, _3);
  not not_12 (not_12_out, _2);
  not not_13 (not_13_out, _0);
  not not_14 (not_14_out, _3);
  not not_15 (not_15_out, _2);
  not not_16 (not_16_out, _1);
  and and_1 (_1_2, not_1_out, not_2_out, not_3_out, not_4_out);
  and and_2 (_4, _3, not_5_out, not_6_out, not_7_out);
  and and_3 (_5, not_8_out, _2, not_9_out, not_10_out);
  and and_4 (_7, not_11_out, not_12_out, _1, not_13_out);
  and and_5 (_8, not_14_out, not_15_out, not_16_out, _0);
  or or_1 (_2_2, _1_2, _4);
  or or_2 (_3_2, _4, _5);

  assign _6 = _4;
  assign _9 = _1_2;
  assign _10 = _7;
endmodule

module main (
  output [23:0] out_1,
  output out_2,
  output [23:0] out_3,
  output [23:0] out_4,
  output [23:0] out_5
);

  wire alucon_1_out_9, and_1_out, clock_1_out, controlunit_1__1_2, controlunit_1__2_2, controlunit_1__3_2,
       controlunit_1__4, controlunit_1__5, controlunit_1__6, controlunit_1__7, controlunit_1__8,
       controlunit_1__9, controlunit_1__10;
  wire [1:0] alucon_1_out_11;
  wire [3:0] multiplexer_1_out;
  wire [19:0] adder_1_out;
  wire [19:16] adder_1_out_2;
  wire [23:0] adder_2_out, bit_extender_1_out, multiplexer_2_out, multiplexer_3_out, multiplexer_4_out,
       ram_1_data, register_1_q;
  wire [23:20] rom_1_data;

  Register #(.width(24)) register_1 (.D(multiplexer_4_out), .Q(register_1_q), .clk(clock_1_out));  // open: en, clr
  Clock clock_1 (.out(clock_1_out));
  Adder #(.width(24)) adder_1 (.a(register_1_q), .b(24'h1), .out({adder_1_out_2, adder_1_out}));  // open: cin, cout
  ROM #(.addrWidth(24), .dataWidth(24)) rom_1 (
    .addr(register_1_q),
    .data({rom_1_data, adder_1_out_2, adder_1_out_2, adder_1_out_2, adder_1_out_2, adder_1_out_2}));  // open: sel
  assign bit_extender_1_out = {{12{adder_1_out_2[19]}}, {adder_1_out_2, adder_1_out_2, adder_1_out_2}};  // Bit_Extender bit_extender_1
  Multiplexer #(.width(4), .enable("false")) multiplexer_1 (
    .in0(adder_1_out_2), .in1(adder_1_out_2), .out(multiplexer_1_out), .sel(controlunit_1__1_2));
  CONTROLUNIT controlunit_1 (
    ._1_2(controlunit_1__1_2), ._2_2(controlunit_1__2_2), ._3_2(controlunit_1__3_2), ._4(controlunit_1__4),
    ._5(controlunit_1__5), ._6(controlunit_1__6), ._7(controlunit_1__7), ._8(controlunit_1__8),
    ._9(controlunit_1__9), ._10(controlunit_1__10), ._3(rom_1_data[23]), ._2(rom_1_data[22]),
    ._1(rom_1_data[21]), ._0(rom_1_data[20]));
  RegFile regfile_1 (
    .in_1(out_3), .write_data(controlunit_1__2_2), .out_7(out_1), .out_8(out_4), .in_4(multiplexer_1_out),
    .clk(clock_1_out), .in_5(adder_1_out_2), .in_3(adder_1_out_2));
  ALUCON alucon_1 (
    ._0(adder_1_out_2[16]), .out_9(alucon_1_out_9), .out_10(alucon_1_out_11[1]), .out_11(alucon_1_out_11[0]),
    .in_2(controlunit_1__9), .in_3(controlunit_1__10), .F3(adder_1_out_2[19]), .F2(adder_1_out_2[18]),
    .F1(adder_1_out_2[17]), .F0(adder_1_out_2[16]));  // open: out_8
  Multiplexer #(.width(24), .enable("false")) multiplexer_2 (
    .in0(out_4), .in1(bit_extender_1_out), .out(multiplexer_2_out), .sel(controlunit_1__3_2));
  Adder #(.width(24)) adder_2 (
    .a({adder_1_out_2, adder_1_out}), .b(bit_extender_1_out), .out(adder_2_out));  // open: cin, cout
  ALU alu_1 (
    .in_1(out_1), .in_2(multiplexer_2_out), .Zero_Flag(out_2), .out_6(out_5), .B_Invert(alucon_1_out_9),
    .ALU_Control_Bits(alucon_1_out_11));
  Multiplexer #(.width(24), .enable("false")) multiplexer_3 (
    .in0({adder_1_out_2, adder_1_out}), .in1(adder_2_out), .out(multiplexer_3_out), .sel(and_1_out));
  and and_1 (and_1_out, controlunit_1__7, out_2);
  Multiplexer #(.width(24), .enable("false")) multiplexer_4 (
    .in0(multiplexer_3_out),
    .in1({adder_1_out_2, adder_1_out_2, adder_1_out_2, adder_1_out_2, adder_1_out_2, adder_1_out_2}),
    .out(multiplexer_4_out), .sel(controlunit_1__8));
  Multiplexer #(.width(24), .enable("false")) multiplexer_5 (
    .in0(out_5), .in1(ram_1_data), .out(out_3), .sel(controlunit_1__6));
  RAM #(.addrWidth(24), .dataWidth(24), .bus("separate")) ram_1 (
    .addr(out_5), .data(ram_1_data), .str(controlunit_1__5), .clk(clock_1_out), .ld(controlunit_1__4));  // open: din, sel, clr

  // Notes on the sheet:
  //   FN
  //   contents of rom_1 (hex, n*v repeats v):
  //   123123
  //   OP
endmodule
